# Fritzing sketch TMB-DataRead (saved by Fritzing 1.0.2b)
breadboards: 1

parts:
  Part1 = Arduino Mega ADK (Rev3)
  U1 = LCD-16X2 [package=lcd-16x2]

nets:
  N1: Part1.A5, U1.DB2
  GND: Part1.GND, U1.VSS
  N2: Part1.D5_PWM, U1.DB3

notes:
  MB-TMB880CF-1
  To Oscillosope ==>
  Reading Data From a
  TMB Temperature Module
  Data
  Clock
  GND
